// Logisim project s-mips.circ as structural Verilog: 6 circuits, main circuit S-MIPS Board
module S_MIPS_Board (
  output halt
);

  wire button_1_out, CLK, CS, d_ff_1_q, R_W, Reset_out, RST, TTY_EN;
  wire [2:0] KDB;
  wire [3:0] Mask, ram_1_read_time, ram_1_write_time;
  wire [6:0] KDB_DATA, TTY_DATA;
  wire [15:0] Addr;
  wire [31:0] ram_1_data_out_0, ram_1_data_out_1, ram_1_data_out_2, ram_1_data_out_3, s_mips_1_ram_in_0,
       s_mips_1_ram_in_1, s_mips_1_ram_in_2, s_mips_1_ram_in_3;

  TTY #(.rows(25), .cols(80)) tty_1 (.data(TTY_DATA), .clk(CLK), .we(TTY_EN), .clr(RST));
  RAM ram_1 (
    .Address(Addr), .Data_Out_0(ram_1_data_out_0), .Data_Out_1(ram_1_data_out_1),
    .Data_Out_2(ram_1_data_out_2), .Data_Out_3(ram_1_data_out_3), .Data_In_0(s_mips_1_ram_in_0),
    .Data_In_1(s_mips_1_ram_in_1), .Data_In_2(s_mips_1_ram_in_2), .Data_In_3(s_mips_1_ram_in_3), .Mask(Mask),
    .nRead_Write(R_W), .Chip_Select(CS), .Read_Time(ram_1_read_time), .Reset(button_1_out),
    .Write_Time(ram_1_write_time));
  Button button_1 (.out(button_1_out));
  Keyboard #(.buflen(64)) keyboard_1 (.clk(CLK), .re(KDB[0]), .avail(KDB[2]), .data(KDB_DATA));  // open: clr
  S_MIPS s_mips_1 (
    .Kbd_Enable(KDB[0]), .Address(Addr), .Kbd_Clear(KDB[1]), .Kbd_Available(KDB[2]),
    .RAM_In_0(s_mips_1_ram_in_0), .Kbd_ASCII_Data(KDB_DATA), .RAM_In_1(s_mips_1_ram_in_1),
    .TTY_Enable(TTY_EN), .RAM_In_2(s_mips_1_ram_in_2), .RAM_In_3(s_mips_1_ram_in_3),
    .TTY_ASCII_Data(TTY_DATA), .Reset(RST), .RAM_Out_0(ram_1_data_out_0), .Clock(CLK),
    .RAM_Out_1(ram_1_data_out_1), .Stop(halt), .RAM_Out_2(ram_1_data_out_2), .RAM_Out_3(ram_1_data_out_3),
    .Mask(Mask), .Read_Time(ram_1_read_time), .Write_Time(ram_1_write_time), .nRead_Write(R_W),
    .Chip_Select(CS));
  D_Flip_Flop d_ff_1 (.clk(CLK), .D(1'b1), .Q(d_ff_1_q), .reset(Reset_out));  // open: Qn, preset, en
  Button Reset (.out(Reset_out));
  Clock clock_1 (.out(CLK));
  D_Flip_Flop d_ff_2 (.clk(CLK), .D(d_ff_1_q), .Qn(RST), .reset(Reset_out));  // open: Q, preset, en

  // Notes on the sheet:
  //   NO MODIFICAR
  //   Keyboard
endmodule

module RAM (
  input  [15:0] Address,
  input  [31:0] Data_In_0,
  input  [31:0] Data_In_1,
  input  [31:0] Data_In_2,
  input  [31:0] Data_In_3,
  input  [3:0] Mask,
  input  nRead_Write,
  input  Chip_Select,
  input  Reset,
  output [31:0] Data_Out_0,
  output [31:0] Data_Out_1,
  output [31:0] Data_Out_2,
  output [31:0] Data_Out_3,
  output [3:0] Read_Time,
  output [3:0] Write_Time
);

  wire and_2_out, and_3_out, and_4_out, and_5_out, and_6_out, and_7_out, and_8_out, and_9_out, Changed, CLK,
       comparator_2_eq, comparator_3_eq, comparator_4_eq, comparator_5_eq, comparator_6_eq, Count,
       demultiplexer_3_out0, Idle, Idle_q, Load, Load0, Load1, nand_1_out, or_1_out, or_2_out, or_3_out,
       or_4_out, or_5_out, or_6_out, or_7_out, or_8_out, or_9_out, or_10_out, Proc_q, Update_Mem, Zero_Time;
  wire [3:0] counter_1_q, multiplexer_1_out, subtractor_1_out;
  wire [31:0] register_1_q, register_2_q, register_3_q, register_4_q, register_5_q;

  // Probe on 4'b0011
  // Probe on 4'b0101
  Multiplexer #(.width(4), .enable("false")) multiplexer_1 (
    .in0(4'b0011), .in1(4'b0101), .out(multiplexer_1_out), .sel(nRead_Write));
  or or_1 (or_1_out, Idle, Update_Mem);
  or or_2 (or_2_out, ~Chip_Select, Reset);  // OR_Gate
  Subtractor #(.width(4)) subtractor_1 (.a(multiplexer_1_out), .b(4'b0010), .out(subtractor_1_out));  // open: bin, bout
  Demultiplexer #(.enable("false")) demultiplexer_1 (.out0(Idle), .out1(Load0), .in(Idle_q), .sel(Changed));
  D_Flip_Flop u_Idle (.clk(CLK), .D(or_1_out), .Q(Idle_q), .preset(or_2_out));  // open: Qn, en, reset
  // Probe on counter_1_q
  Counter #(.width(4), .max('hf)) counter_1 (
    .load(Load), .D(subtractor_1_out), .count(Count), .Q(counter_1_q), .clk(CLK), .clr(or_3_out));  // open: carry
  or or_3 (or_3_out, ~Chip_Select, Reset);  // OR_Gate
  Comparator #(.width(4), .mode("unsigned")) comparator_1 (
    .a(4'b0000), .b(counter_1_q), .eq(Zero_Time));  // open: gt, lt
  or or_4 (or_4_out, Count, Load0, Load1);
  Register #(.width(32)) register_1 (.D(Data_In_0), .en(Chip_Select), .Q(register_1_q), .clk(CLK), .clr(or_5_out));
  or or_5 (or_5_out, ~Chip_Select, Reset);  // OR_Gate
  Register #(.width(32)) register_2 (.D(Data_In_1), .en(Chip_Select), .Q(register_2_q), .clk(CLK), .clr(or_6_out));
  or or_6 (or_6_out, ~Chip_Select, Reset);  // OR_Gate
  Register #(.width(32)) register_3 (.D(Data_In_2), .en(Chip_Select), .Q(register_3_q), .clk(CLK), .clr(or_7_out));
  or or_7 (or_7_out, ~Chip_Select, Reset);  // OR_Gate
  Register #(.width(32)) register_4 (.D(Data_In_3), .en(Chip_Select), .Q(register_4_q), .clk(CLK), .clr(or_8_out));
  or or_8 (or_8_out, ~Chip_Select, Reset);  // OR_Gate
  Register #(.width(32)) register_5 (
    .D({{11{1'b1}}, nRead_Write, Mask, Address}), .en(Chip_Select), .Q(register_5_q), .clk(CLK),
    .clr(or_9_out));
  or or_9 (or_9_out, ~Chip_Select, Reset);  // OR_Gate
  D_Flip_Flop Proc (.clk(CLK), .D(or_4_out), .Q(Proc_q), .reset(or_10_out));  // open: Qn, preset, en
  or or_10 (or_10_out, ~Chip_Select, Reset);  // OR_Gate
  Demultiplexer #(.enable("false")) demultiplexer_2 (
    .out0(Count), .out1(Update_Mem), .in(demultiplexer_3_out0), .sel(Zero_Time));
  Demultiplexer #(.enable("false")) demultiplexer_3 (
    .out0(demultiplexer_3_out0), .out1(Load1), .in(Proc_q), .sel(Changed));
  Clock clock_1 (.out(CLK));
  Comparator #(.width(32)) comparator_2 (.a(register_1_q), .b(Data_In_0), .eq(comparator_2_eq));  // open: gt, lt
  Comparator #(.width(32)) comparator_3 (.a(register_2_q), .b(Data_In_1), .eq(comparator_3_eq));  // open: gt, lt
  Comparator #(.width(32)) comparator_4 (.a(register_3_q), .b(Data_In_2), .eq(comparator_4_eq));  // open: gt, lt
  Comparator #(.width(32)) comparator_5 (.a(register_4_q), .b(Data_In_3), .eq(comparator_5_eq));  // open: gt, lt
  Comparator #(.width(32)) comparator_6 (
    .a(register_5_q), .b({{11{1'b1}}, nRead_Write, Mask, Address}), .eq(comparator_6_eq));  // open: gt, lt
  nand nand_1 (nand_1_out, comparator_6_eq, comparator_2_eq, comparator_3_eq, comparator_4_eq, comparator_5_eq);
  and and_1 (Changed, nand_1_out, Chip_Select);
  or or_11 (Load, Count, Load1, Load0);
  and and_2 (and_2_out, Mask[0], Update_Mem, nRead_Write);
  and and_3 (and_3_out, Mask[1], Update_Mem, nRead_Write);
  and and_4 (and_4_out, Mask[2], Update_Mem, nRead_Write);
  and and_5 (and_5_out, Mask[3], Update_Mem, nRead_Write);
  RAM_part #(.addrWidth(16), .dataWidth(32), .bus("separate")) ram_1 (
    .addr(Address), .din(Data_In_0), .data(Data_Out_0), .str(and_2_out), .sel(Chip_Select), .clk(CLK),
    .ld(and_6_out), .clr(Reset));
  and and_6 (and_6_out, ~nRead_Write, Idle);  // AND_Gate
  RAM_part #(.addrWidth(16), .dataWidth(32), .bus("separate")) ram_2 (
    .addr(Address), .din(Data_In_1), .data(Data_Out_1), .str(and_3_out), .sel(Chip_Select), .clk(CLK),
    .ld(and_7_out), .clr(Reset));
  and and_7 (and_7_out, ~nRead_Write, Idle);  // AND_Gate
  RAM_part #(.addrWidth(16), .dataWidth(32), .bus("separate")) ram_3 (
    .addr(Address), .din(Data_In_2), .data(Data_Out_2), .str(and_4_out), .sel(Chip_Select), .clk(CLK),
    .ld(and_8_out), .clr(Reset));
  and and_8 (and_8_out, ~nRead_Write, Idle);  // AND_Gate
  RAM_part #(.addrWidth(16), .dataWidth(32), .bus("separate")) ram_4 (
    .addr(Address), .din(Data_In_3), .data(Data_Out_3), .str(and_5_out), .sel(Chip_Select), .clk(CLK),
    .ld(and_9_out), .clr(Reset));
  and and_9 (and_9_out, ~nRead_Write, Idle);  // AND_Gate

  assign Read_Time = 4'b0011;
  assign Write_Time = 4'b0101;

  // Other names for the same wires on the sheet: M0 = Mask[0]; M1 = Mask[1]; M2 = Mask[2]; M3 = Mask[3];
  //   RW = nRead_Write; CLR = Reset; CS = Chip_Select; Load2 = Count

  // Notes on the sheet:
  //   NO MODIFICAR
  //   excepto quizás los valores RT y WT
  //   BANK0
  //   BANK1
  //   BANK2
  //   BANK3
endmodule

module S_MIPS (
  input  Kbd_Available,
  input  [6:0] Kbd_ASCII_Data,
  input  [31:0] RAM_Out_0,
  input  [31:0] RAM_Out_1,
  input  Reset,
  input  [31:0] RAM_Out_2,
  input  Clock,
  input  [31:0] RAM_Out_3,
  input  [3:0] Read_Time,
  input  [3:0] Write_Time,
  output Kbd_Enable,
  output [15:0] Address,
  output Kbd_Clear,
  output TTY_Enable,
  output [6:0] TTY_ASCII_Data,
  output Stop,
  output [31:0] RAM_In_0,
  output [31:0] RAM_In_1,
  output [31:0] RAM_In_2,
  output [31:0] RAM_In_3,
  output [3:0] Mask,
  output nRead_Write,
  output Chip_Select
);


  assign Address = {16{1'b0}};
  assign Chip_Select = 1'b0;
  assign Kbd_Clear = 1'b0;
  assign Kbd_Enable = 1'b0;
  assign Mask = 4'b0000;
  assign nRead_Write = 1'b0;
  assign RAM_In_0 = {32{1'b0}};
  assign RAM_In_1 = {32{1'b0}};
  assign RAM_In_2 = {32{1'b0}};
  assign RAM_In_3 = {32{1'b0}};
  assign Stop = 1'b0;
  assign TTY_Enable = 1'b0;

  // Other names for the same wires on the sheet: CLK = Clock; CLR = Reset; KBD_AVAIL = Kbd_Available;
  //   KBD_DATA[6:0] = Kbd_ASCII_Data; RAM_OUTPUT_0[31:0] = RAM_Out_0; RAM_OUTPUT_1[31:0] = RAM_Out_1;
  //   RAM_OUTPUT_2[31:0] = RAM_Out_2; RAM_OUTPUT_3[31:0] = RAM_Out_3; TTY_DATA[6:0] = TTY_ASCII_Data

  // Notes on the sheet:
  //   RAM ADDRESS
  //   DATA FROM RAM
  //   DATA TO RAM
  //   DATA WRITE MASK
  //   RAM TIMING
  //   RAM CONTROL
  //   KEYBOARD
  //   TTY
  //   SEQUENCING
  //   Esto lo tienen que borrar:
endmodule

module RegisterFile (
  input  [4:0] \Dirección_de_destino ,
  input  Read_Write,
  input  [31:0] Datos_de_entrada,
  input  [4:0] Selector_de_salida_A,
  input  [4:0] Selector_de_salida_B,
  input  Reset,
  input  Clock,
  output [31:0] Read_Data_1,
  output [31:0] Read_Data_2
);

  wire Register_0_on_off, Register_1_on_off, Register_2_on_off, Register_3_on_off, Register_4_on_off,
       Register_5_on_off, Register_6_on_off, Register_7_on_off, Register_8_on_off, Register_9_on_off,
       Register_10_on_off, Register_11_on_off, Register_12_on_off, Register_13_on_off, Register_14_on_off,
       Register_15_on_off, Register_16_on_off, Register_17_on_off, Register_18_on_off, Register_19_on_off,
       Register_20_on_off, Register_21_on_off, Register_22_on_off, Register_23_on_off, Register_24_on_off,
       Register_25_on_off, Register_26_on_off, Register_27_on_off, Register_28_on_off, Register_29_on_off,
       Register_30_on_off, Register_31_on_off;
  wire [31:0] reg0_out, reg1_out, reg2_out, reg3_out, reg3out, reg4_out, reg5_out, reg6_out, reg7_out,
       reg8_out, reg9_out, reg10_out, reg11_out, reg12_out, reg13_out, reg14_out, reg15_out, reg16_out,
       reg17_out, reg18_out, reg19_out, reg20_out, reg21_out, reg22_out, reg23_out, reg24_out, reg25_out,
       reg26_out, reg27_out, reg28_out, reg29_out, reg30_out, reg30_ut, reg31_out;

  Register #(.width(32)) register_1 (.D({32{1'b0}}), .en(Register_0_on_off), .Q(reg0_out), .clk(Clock), .clr(Reset));
  Register #(.width(32)) register_2 (
    .D(Datos_de_entrada), .en(Register_1_on_off), .Q(reg1_out), .clk(Clock), .clr(Reset));
  Register #(.width(32)) register_3 (
    .D(Datos_de_entrada), .en(Register_2_on_off), .Q(reg2_out), .clk(Clock), .clr(Reset));
  Register #(.width(32)) register_4 (
    .D(Datos_de_entrada), .en(Register_3_on_off), .Q(reg3out), .clk(Clock), .clr(Reset));
  Register #(.width(32)) register_5 (
    .D(Datos_de_entrada), .en(Register_4_on_off), .Q(reg4_out), .clk(Clock), .clr(Reset));
  Register #(.width(32)) register_6 (
    .D(Datos_de_entrada), .en(Register_5_on_off), .Q(reg5_out), .clk(Clock), .clr(Reset));
  Register #(.width(32)) register_7 (
    .D(Datos_de_entrada), .en(Register_6_on_off), .Q(reg6_out), .clk(Clock), .clr(Reset));
  Register #(.width(32)) register_8 (
    .D(Datos_de_entrada), .en(Register_7_on_off), .Q(reg7_out), .clk(Clock), .clr(Reset));
  Register #(.width(32)) register_9 (
    .D(Datos_de_entrada), .en(Register_8_on_off), .Q(reg8_out), .clk(Clock), .clr(Reset));
  Register #(.width(32)) register_10 (
    .D(Datos_de_entrada), .en(Register_9_on_off), .Q(reg9_out), .clk(Clock), .clr(Reset));
  Register #(.width(32)) register_11 (
    .D(Datos_de_entrada), .en(Register_10_on_off), .Q(reg10_out), .clk(Clock), .clr(Reset));
  Register #(.width(32)) register_12 (
    .D(Datos_de_entrada), .en(Register_11_on_off), .Q(reg11_out), .clk(Clock), .clr(Reset));
  Register #(.width(32)) register_13 (
    .D(Datos_de_entrada), .en(Register_12_on_off), .Q(reg12_out), .clk(Clock), .clr(Reset));
  Register #(.width(32)) register_14 (
    .D(Datos_de_entrada), .en(Register_13_on_off), .Q(reg13_out), .clk(Clock), .clr(Reset));
  Register #(.width(32)) register_15 (
    .D(Datos_de_entrada), .en(Register_14_on_off), .Q(reg14_out), .clk(Clock), .clr(Reset));
  Register #(.width(32)) register_16 (
    .D(Datos_de_entrada), .en(Register_15_on_off), .Q(reg15_out), .clk(Clock), .clr(Reset));
  Register #(.width(32)) register_17 (
    .D(Datos_de_entrada), .en(Register_16_on_off), .Q(reg16_out), .clk(Clock), .clr(Reset));
  Register #(.width(32)) register_18 (
    .D(Datos_de_entrada), .en(Register_17_on_off), .Q(reg17_out), .clk(Clock), .clr(Reset));
  Register #(.width(32)) register_19 (
    .D(Datos_de_entrada), .en(Register_16_on_off), .Q(reg18_out), .clk(Clock), .clr(Reset));
  Register #(.width(32)) register_20 (
    .D(Datos_de_entrada), .en(Register_17_on_off), .Q(reg19_out), .clk(Clock), .clr(Reset));
  Register #(.width(32)) register_21 (
    .D(Datos_de_entrada), .en(Register_20_on_off), .Q(reg20_out), .clk(Clock), .clr(Reset));
  Register #(.width(32)) register_22 (
    .D(Datos_de_entrada), .en(Register_21_on_off), .Q(reg21_out), .clk(Clock), .clr(Reset));
  Register #(.width(32)) register_23 (
    .D(Datos_de_entrada), .en(Register_22_on_off), .Q(reg22_out), .clk(Clock), .clr(Reset));
  Register #(.width(32)) register_24 (
    .D(Datos_de_entrada), .en(Register_23_on_off), .Q(reg23_out), .clk(Clock), .clr(Reset));
  Register #(.width(32)) register_25 (
    .D(Datos_de_entrada), .en(Register_24_on_off), .Q(reg24_out), .clk(Clock), .clr(Reset));
  Register #(.width(32)) register_26 (
    .D(Datos_de_entrada), .en(Register_25_on_off), .Q(reg25_out), .clk(Clock), .clr(Reset));
  Register #(.width(32)) register_27 (
    .D(Datos_de_entrada), .en(Register_26_on_off), .Q(reg26_out), .clk(Clock), .clr(Reset));
  Register #(.width(32)) register_28 (
    .D(Datos_de_entrada), .en(Register_27_on_off), .Q(reg27_out), .clk(Clock), .clr(Reset));
  Register #(.width(32)) register_29 (
    .D(Datos_de_entrada), .en(Register_28_on_off), .Q(reg28_out), .clk(Clock), .clr(Reset));
  Register #(.width(32)) register_30 (
    .D(Datos_de_entrada), .en(Register_29_on_off), .Q(reg29_out), .clk(Clock), .clr(Reset));
  Register #(.width(32)) register_31 (
    .D(Datos_de_entrada), .en(Register_30_on_off), .Q(reg30_ut), .clk(Clock), .clr(Reset));
  Register #(.width(32)) register_32 (
    .D(Datos_de_entrada), .en(Register_31_on_off), .Q(reg31_out), .clk(Clock), .clr(Reset));
  Demultiplexer #(.select(5)) demultiplexer_1 (
    .out0(Register_0_on_off), .out1(Register_1_on_off), .out2(Register_2_on_off), .out3(Register_3_on_off),
    .out4(Register_4_on_off), .out5(Register_5_on_off), .out6(Register_6_on_off), .out7(Register_7_on_off),
    .out8(Register_8_on_off), .out9(Register_9_on_off), .out10(Register_10_on_off),
    .out11(Register_11_on_off), .out12(Register_12_on_off), .out13(Register_13_on_off),
    .out14(Register_14_on_off), .out15(Register_15_on_off), .out16(Register_16_on_off),
    .out17(Register_17_on_off), .out18(Register_18_on_off), .out19(Register_19_on_off),
    .out20(Register_20_on_off), .out21(Register_21_on_off), .out22(Register_22_on_off),
    .out23(Register_23_on_off), .out24(Register_24_on_off), .out25(Register_25_on_off),
    .out26(Register_26_on_off), .out27(Register_27_on_off), .out28(Register_28_on_off),
    .out29(Register_29_on_off), .out30(Register_30_on_off), .out31(Register_31_on_off), .in(Read_Write),
    .sel(\Dirección_de_destino ));  // open: en
  Multiplexer #(.select(5), .width(32)) multiplexer_1 (
    .in0(reg0_out), .in1(reg1_out), .in2(reg2_out), .in3(reg3_out), .in4(reg4_out), .in5(reg5_out),
    .in6(reg6_out), .in7(reg7_out), .in8(reg8_out), .in9(reg9_out), .in10(reg10_out), .in11(reg11_out),
    .in12(reg12_out), .in13(reg13_out), .in14(reg14_out), .in15(reg15_out), .in16(reg16_out),
    .in17(reg17_out), .in18(reg18_out), .in19(reg19_out), .in20(reg20_out), .in21(reg21_out),
    .in22(reg22_out), .in23(reg23_out), .in24(reg24_out), .in25(reg25_out), .in26(reg26_out),
    .in27(reg27_out), .in28(reg28_out), .in29(reg29_out), .in30(reg30_out), .in31(reg31_out),
    .out(Read_Data_1), .sel(Selector_de_salida_A));  // open: en
  Multiplexer #(.select(5), .width(32)) multiplexer_2 (
    .in0(reg0_out), .in1(reg1_out), .in2(reg2_out), .in3(reg3_out), .in4(reg4_out), .in5(reg5_out),
    .in6(reg6_out), .in7(reg7_out), .in8(reg8_out), .in9(reg9_out), .in10(reg10_out), .in11(reg11_out),
    .in12(reg12_out), .in13(reg13_out), .in14(reg14_out), .in15(reg15_out), .in16(reg16_out),
    .in17(reg17_out), .in18(reg18_out), .in19(reg19_out), .in20(reg20_out), .in21(reg21_out),
    .in22(reg22_out), .in23(reg23_out), .in24(reg24_out), .in25(reg25_out), .in26(reg26_out),
    .in27(reg27_out), .in28(reg28_out), .in29(reg29_out), .in30(reg30_out), .in31(reg31_out),
    .out(Read_Data_2), .sel(Selector_de_salida_B));  // open: en

  // Other names for the same wires on the sheet: clk = Clock; input_value[31:0] = Datos_de_entrada; R_W = Read_Write;
  //   read_dataA[31:0] = Read_Data_1; read_dataB[31:0] = Read_Data_2; read_regA[4:0] = Selector_de_salida_A;
  //   read_regB[4:0] = Selector_de_salida_B; write_reg[4:0] = \Dirección_de_destino 

  // Notes on the sheet:
  //   Inputs
  //   OUTPUTS from your circuit
endmodule

module DataPath (
  input  [4:0] Register_A,
  input  [4:0] Register_B,
  input  Read_Write,
  input  [4:0] Write_addres,
  input  Clock,
  input  [2:0] Instruction,
  output Overflow,
  output Neg,
  output Zero,
  output Carry
);

  wire [31:0] registerfile_1_read_data_1, registerfile_1_read_data_2;

  RegisterFile registerfile_1 (
    .\Dirección_de_destino (Write_addres), .Read_Write(Read_Write), .Selector_de_salida_A(Register_A),
    .Selector_de_salida_B(Register_B), .Clock(Clock), .Read_Data_1(registerfile_1_read_data_1),
    .Read_Data_2(registerfile_1_read_data_2));  // open: Datos_de_entrada, Reset
  ALU alu_1 (
    .Op1(registerfile_1_read_data_1), .Op2(registerfile_1_read_data_2), .Instruction(Instruction),
    .Carry(Carry), .Zero(Zero), .Neg(Neg), .Overflow(Overflow));  // open: Auxiliar_Reg, Result
endmodule

module ALU (
  input  [31:0] Op1,
  input  [31:0] Op2,
  input  [2:0] Instruction,
  output [31:0] Auxiliar_Reg,
  output [31:0] Result,
  output Carry,
  output Zero,
  output Neg,
  output Overflow
);

  wire adder_1_cout, and_2_out, and_3_out, and_4_out, and_5_out, and_6_out, and_7_out, comparator_1_eq,
       comparator_2_eq, subtractor_1_bout, xor_1_out, xor_2_out, xor_3_out, xor_4_out;
  wire [31:0] and_1_out, div, mult, multiplier_1_cout, not_1_out, not_2_out, or_1_out, reminder, sub, sum,
       undriven;

  Adder #(.width(32)) adder_1 (.a(Op1), .b(Op2), .out(sum), .cin(1'b0), .cout(adder_1_cout));
  Subtractor #(.width(32)) subtractor_1 (.a(Op1), .b(Op2), .out(sub), .bin(1'b0), .bout(subtractor_1_bout));
  Multiplier #(.width(32)) multiplier_1 (.a(Op1), .b(Op2), .out(mult), .cout(multiplier_1_cout));  // open: cin
  Divider #(.width(32)) divider_1 (.a(Op1), .b(Op2), .out(div), .upper(undriven), .rem(reminder));
  assign and_1_out = Op1 & Op2;  // AND_Gate and_1, 32 bits wide
  assign or_1_out = Op1 | Op2;  // OR_Gate or_1, 32 bits wide
  assign not_1_out = ~Op1;  // NOT_Gate not_1, 32 bits wide
  xor xor_1 (xor_1_out, Op1[31], sum[31]);
  xor xor_2 (xor_2_out, sum[31], Op2[31]);
  xor xor_3 (xor_3_out, Op1[31], sub[31]);
  xor xor_4 (xor_4_out, sub[31], Op2[31]);
  and and_2 (and_2_out, xor_1_out, xor_2_out);
  and and_3 (and_3_out, xor_3_out, xor_4_out);
  Comparator #(.width(3)) comparator_1 (.a(Instruction), .b(3'b000), .eq(comparator_1_eq));  // open: gt, lt
  Comparator #(.width(3)) comparator_2 (.a(Instruction), .b(3'b001), .eq(comparator_2_eq));  // open: gt, lt
  Multiplexer #(.select(3), .width(32), .enable("false")) multiplexer_1 (
    .in0({32{1'b0}}), .in1({32{1'b0}}), .in2(multiplier_1_cout), .in3(undriven), .in4({32{1'b0}}),
    .in5({32{1'b0}}), .in6({32{1'b0}}), .in7(not_2_out), .out(Auxiliar_Reg), .sel(Instruction));
  assign not_2_out = ~Op2;  // NOT_Gate not_2, 32 bits wide
  Multiplexer #(.select(3), .width(32), .enable("false")) multiplexer_2 (
    .in0(sum), .in1(sub), .in2(mult), .in3(div), .in4(reminder), .in5(and_1_out), .in6(or_1_out),
    .in7(not_1_out), .out(Result), .sel(Instruction));
  and and_4 (and_4_out, and_2_out, comparator_1_eq);
  and and_5 (and_5_out, comparator_1_eq, adder_1_cout);
  or or_2 (Carry, and_5_out, and_6_out);
  and and_6 (and_6_out, subtractor_1_bout, comparator_2_eq);
  and and_7 (and_7_out, comparator_2_eq, and_3_out);
  Comparator #(.width(32)) comparator_3 (.a(Result), .b({32{1'b0}}), .eq(Zero), .lt(Neg));  // open: gt
  or or_3 (Overflow, and_4_out, and_7_out);

  // Other names for the same wires on the sheet: auxiliar[31:0] = Auxiliar_Reg; opA[31:0] = Op1; opB[31:0] = Op2;
  //   Overflow_flag = Overflow; S[2:0] = Instruction

  // Notes on the sheet:
  //   INPUTS
  //   Outputs
  //   Flags
endmodule
